# Fritzing sketch Schematics (saved by Fritzing 0.9.3b)
breadboards: 1

parts:
  Arduino_Nano_v3 = Arduino Nano (Rev3.0)
  2N3904 = NPN-Transistor [package="TO92 [THT]"]
  R5 = Resistor [tolerance=±5% resistance=100k package=THT]
  R6 = Resistor [tolerance=±5% resistance=2.2k package=THT]
  R1 = Resistor [tolerance=±5% resistance=10k package=THT]
  Move_Up_Button = Pushbutton [package="[THT]"]
  R7 = Resistor [tolerance=±5% resistance=10k package=THT]
  Mem_1_Button = Pushbutton [package="[THT]"]
  R8 = Resistor [tolerance=±5% resistance=10k package=THT]
  Mem_2_Button = Pushbutton [package="[THT]"]
  R9 = Resistor [tolerance=±5% resistance=10k package=THT]
  Move_Down_Button = Pushbutton [package="[THT]"]

nets:
  Common Ground/GND: Arduino_Nano_v3.GND, 2N3904.E, R1.Pin_0, R7.Pin_0, R8.Pin_0, R9.Pin_0
  D2: Arduino_Nano_v3.D2
  N1: Arduino_Nano_v3.D3, R1.Pin_1, Move_Up_Button.Pin_3, Move_Up_Button.Pin_4
  MoveUpControl: Arduino_Nano_v3.D4
  N2: Arduino_Nano_v3.D5, R7.Pin_1, Mem_1_Button.Pin_3, Mem_1_Button.Pin_4
  N3: Arduino_Nano_v3.D6, R8.Pin_1, Mem_2_Button.Pin_3, Mem_2_Button.Pin_4
  MoveDownControl: Arduino_Nano_v3.D7
  N4: Arduino_Nano_v3.D8, R9.Pin_1, Move_Down_Button.Pin_3, Move_Down_Button.Pin_4
  12V: Arduino_Nano_v3.VIN
  5V: Arduino_Nano_v3.5V, R6.Pin_0, Move_Up_Button.Pin_1, Move_Up_Button.Pin_2, Mem_1_Button.Pin_1, Mem_2_Button.Pin_1, Move_Down_Button.Pin_1, Move_Down_Button.Pin_2
  N5: 2N3904.B, R5.Pin_1
  N6: 2N3904.C, R6.Pin_1
  LIN Signal: R5.Pin_0

notes:
  Buck Converter Output
